// Logisim project Lab1_Logisim_Waldmann.circ as structural Verilog: 7 circuits, main circuit main
module main (
  input  [17:0] SW,
  input  s,
  input  [7:0] x,
  input  [7:0] m,
  input  [7:0] y,
  output [17:0] LEDR
);

  mux2to1 mux2to1_1 (.x(x[0]), .y(y[0]), .s(s), .m(m[0]));
  mux2to1 mux2to1_2 (.x(x[1]), .y(y[1]), .s(s), .m(m[1]));
  mux2to1 mux2to1_3 (.x(x[2]), .y(y[2]), .s(s), .m(m[2]));
  mux2to1 mux2to1_4 (.x(x[3]), .y(y[3]), .s(s), .m(m[3]));
  mux2to1 mux2to1_5 (.x(x[4]), .y(y[4]), .s(s), .m(m[4]));
  mux2to1 mux2to1_6 (.x(x[5]), .y(y[5]), .s(s), .m(m[5]));
  mux2to1 mux2to1_7 (.x(x[6]), .y(y[6]), .s(s), .m(m[6]));
  mux2to1 mux2to1_8 (.x(x[7]), .y(y[7]), .s(s), .m(m[7]));

  assign LEDR = SW;
endmodule

module mux2to1 (
  input  x,
  input  y,
  input  s,
  output m
);

  wire and_1_out, and_2_out, not_1_out;

  not not_1 (not_1_out, s);
  and and_1 (and_1_out, x, not_1_out);
  and and_2 (and_2_out, y, s);
  or or_1 (m, and_1_out, and_2_out);
endmodule

module mux5to1 (
  input  u,
  input  v,
  input  s0,
  input  s1,
  input  w,
  input  x,
  input  y,
  input  s2,
  output m
);

  wire mux2to1_1_m, mux2to1_2_m, mux2to1_3_m;

  mux2to1 mux2to1_1 (.x(u), .y(v), .s(s0), .m(mux2to1_1_m));
  mux2to1 mux2to1_2 (.x(w), .y(x), .s(s0), .m(mux2to1_2_m));
  mux2to1 mux2to1_3 (.x(mux2to1_1_m), .y(mux2to1_2_m), .s(s1), .m(mux2to1_3_m));
  mux2to1 mux2to1_4 (.x(mux2to1_3_m), .y(y), .s(s2), .m(m));
endmodule

module bit3_mux5to1 (
  input  [2:0] u,
  input  [2:0] v,
  input  [2:0] w,
  input  [2:0] xM,
  input  [2:0] yM,
  input  s0,
  input  s1,
  input  s2,
  output [2:0] out_9
);

  mux5to1 mux5to1_1 (.u(u[0]), .v(v[0]), .s0(s0), .s1(s1), .w(w[0]), .x(xM[0]), .y(yM[0]), .s2(s2), .m(out_9[0]));
  mux5to1 mux5to1_2 (.u(u[1]), .v(v[1]), .s0(s0), .s1(s1), .w(w[1]), .x(xM[1]), .y(yM[1]), .s2(s2), .m(out_9[1]));
  mux5to1 mux5to1_3 (.u(u[2]), .v(v[2]), .s0(s0), .s1(s1), .w(w[2]), .x(xM[2]), .y(yM[2]), .s2(s2), .m(out_9[2]));
endmodule

module char7seg (
  input  c2,
  input  c1,
  input  c0,
  output o0,
  output o1,
  output o2,
  output o3,
  output o4,
  output o5,
  output o6
);

  wire and_1_out, and_2_out, and_3_out, and_4_out, and_5_out, not_1_out, not_2_out;

  not not_1 (not_1_out, c1);
  not not_2 (not_2_out, c0);
  or or_1 (o0, not_2_out, c2);
  and and_1 (and_1_out, not_1_out, c0);
  and and_2 (and_2_out, c1, not_2_out);
  and and_3 (and_3_out, not_1_out, c0);
  and and_4 (and_4_out, c1, not_2_out);
  and and_5 (and_5_out, not_1_out, not_2_out);
  or or_2 (o6, c1, c2);
  or or_3 (o1, and_1_out, and_2_out, c2);
  or or_4 (o2, and_3_out, and_4_out, c2);
  or or_5 (o3, and_5_out, c2);

  assign o4 = c2;
  assign o5 = c2;
endmodule

module part5 (
  input  [2:0] u,
  input  [2:0] v,
  input  [2:0] w,
  input  [2:0] xM,
  input  [2:0] yM,
  input  s0,
  input  s1,
  input  s2
);

  wire char7seg_1_o0, char7seg_1_o1, char7seg_1_o2, char7seg_1_o3, char7seg_1_o4, char7seg_1_o5,
       char7seg_1_o6, char7seg_2_o0, char7seg_2_o1, char7seg_2_o2, char7seg_2_o3, char7seg_2_o4,
       char7seg_2_o5, char7seg_2_o6, char7seg_3_o0, char7seg_3_o1, char7seg_3_o2, char7seg_3_o3,
       char7seg_3_o4, char7seg_3_o5, char7seg_3_o6, char7seg_4_o0, char7seg_4_o1, char7seg_4_o2,
       char7seg_4_o3, char7seg_4_o4, char7seg_4_o5, char7seg_4_o6, char7seg_5_o0, char7seg_5_o1,
       char7seg_5_o2, char7seg_5_o3, char7seg_5_o4, char7seg_5_o5, char7seg_5_o6, char7seg_6_o0,
       char7seg_6_o1, char7seg_6_o2, char7seg_6_o3, char7seg_6_o4, char7seg_6_o5, char7seg_6_o6,
       char7seg_7_o0, char7seg_7_o1, char7seg_7_o2, char7seg_7_o3, char7seg_7_o4, char7seg_7_o5,
       char7seg_7_o6, char7seg_8_o0, char7seg_8_o1, char7seg_8_o2, char7seg_8_o3, char7seg_8_o4,
       char7seg_8_o5, char7seg_8_o6, o0, o01, o1, o02, o2, o03, o3, o04, o4, o05, o5, o06, o6, o07, o11, o12,
       o13, o14, o15, o16, o17, o21, o22, o23, o24, o25, o26, o27, o31, o32, o33, o34, o35, o36, o37, o41,
       o42, o43, o44, o45, o46, o47, o51, o52, o53, o54, o55, o56, o57, o61, o62, o63, o64, o65, o66, o67,
       undriven, undriven_2, undriven_3, undriven_4, undriven_5, undriven_6, undriven_7, undriven_8;
  wire [2:0] bit3_mux5to1_1_out_9, bit3_mux5to1_2_out_9, bit3_mux5to1_3_out_9, bit3_mux5to1_4_out_9,
       bit3_mux5to1_5_out_9, bit3_mux5to1_6_out_9, bit3_mux5to1_7_out_9, bit3_mux5to1_8_out_9;

  bit3_mux5to1 bit3_mux5to1_1 (
    .u(u), .v(v), .w(w), .xM(xM), .yM(yM), .s0(s0), .s1(s1), .s2(s2), .out_9(bit3_mux5to1_1_out_9));
  bit3_mux5to1 bit3_mux5to1_2 (
    .u(v), .v(w), .w(xM), .xM(yM), .yM(u), .s0(s0), .s1(s1), .s2(s2), .out_9(bit3_mux5to1_2_out_9));
  bit3_mux5to1 bit3_mux5to1_3 (
    .u(w), .v(xM), .w(yM), .xM(u), .yM(v), .s0(s0), .s1(s1), .s2(s2), .out_9(bit3_mux5to1_3_out_9));
  bit3_mux5to1 bit3_mux5to1_4 (
    .u(xM), .v(yM), .w(u), .xM(v), .yM(w), .s0(s0), .s1(s1), .s2(s2), .out_9(bit3_mux5to1_4_out_9));
  bit3_mux5to1 bit3_mux5to1_5 (
    .u(yM), .v(u), .w(v), .xM(w), .yM(xM), .s0(s0), .s1(s1), .s2(s2), .out_9(bit3_mux5to1_5_out_9));
  bit3_mux5to1 bit3_mux5to1_6 (
    .u(u), .v(v), .w(w), .xM(xM), .yM(yM), .s0(s0), .s1(s1), .s2(s2), .out_9(bit3_mux5to1_6_out_9));
  bit3_mux5to1 bit3_mux5to1_7 (
    .u(v), .v(w), .w(xM), .xM(yM), .yM(u), .s0(s0), .s1(s1), .s2(s2), .out_9(bit3_mux5to1_7_out_9));
  bit3_mux5to1 bit3_mux5to1_8 (
    .u(w), .v(xM), .w(yM), .xM(u), .yM(v), .s0(s0), .s1(s1), .s2(s2), .out_9(bit3_mux5to1_8_out_9));
  not not_1 (o0, char7seg_1_o0);
  char7seg char7seg_1 (
    .c2(bit3_mux5to1_1_out_9[2]), .c1(bit3_mux5to1_1_out_9[1]), .c0(bit3_mux5to1_1_out_9[0]),
    .o0(char7seg_1_o0), .o1(char7seg_1_o1), .o2(char7seg_1_o2), .o3(char7seg_1_o3), .o4(char7seg_1_o4),
    .o5(char7seg_1_o5), .o6(char7seg_1_o6));
  not not_2 (o1, char7seg_1_o1);
  not not_3 (o2, char7seg_1_o2);
  not not_4 (o3, char7seg_1_o3);
  not not_5 (o4, char7seg_1_o4);
  not not_6 (o5, char7seg_1_o5);
  not not_7 (o6, char7seg_1_o6);
  not not_8 (o01, char7seg_2_o0);
  char7seg char7seg_2 (
    .c2(bit3_mux5to1_2_out_9[2]), .c1(bit3_mux5to1_2_out_9[1]), .c0(bit3_mux5to1_2_out_9[0]),
    .o0(char7seg_2_o0), .o1(char7seg_2_o1), .o2(char7seg_2_o2), .o3(char7seg_2_o3), .o4(char7seg_2_o4),
    .o5(char7seg_2_o5), .o6(char7seg_2_o6));
  not not_9 (o11, char7seg_2_o1);
  not not_10 (o21, char7seg_2_o2);
  not not_11 (o31, char7seg_2_o3);
  not not_12 (o41, char7seg_2_o4);
  not not_13 (o51, char7seg_2_o5);
  not not_14 (o61, char7seg_2_o6);
  not not_15 (o02, char7seg_3_o0);
  char7seg char7seg_3 (
    .c2(bit3_mux5to1_3_out_9[2]), .c1(bit3_mux5to1_3_out_9[1]), .c0(bit3_mux5to1_3_out_9[0]),
    .o0(char7seg_3_o0), .o1(char7seg_3_o1), .o2(char7seg_3_o2), .o3(char7seg_3_o3), .o4(char7seg_3_o4),
    .o5(char7seg_3_o5), .o6(char7seg_3_o6));
  not not_16 (o12, char7seg_3_o1);
  not not_17 (o22, char7seg_3_o2);
  not not_18 (o32, char7seg_3_o3);
  not not_19 (o42, char7seg_3_o4);
  not not_20 (o52, char7seg_3_o5);
  not not_21 (o62, char7seg_3_o6);
  not not_22 (o03, char7seg_4_o0);
  char7seg char7seg_4 (
    .c2(bit3_mux5to1_4_out_9[2]), .c1(bit3_mux5to1_4_out_9[1]), .c0(bit3_mux5to1_4_out_9[0]),
    .o0(char7seg_4_o0), .o1(char7seg_4_o1), .o2(char7seg_4_o2), .o3(char7seg_4_o3), .o4(char7seg_4_o4),
    .o5(char7seg_4_o5), .o6(char7seg_4_o6));
  not not_23 (o13, char7seg_4_o1);
  not not_24 (o23, char7seg_4_o2);
  not not_25 (o33, char7seg_4_o3);
  not not_26 (o43, char7seg_4_o4);
  not not_27 (o53, char7seg_4_o5);
  not not_28 (o63, char7seg_4_o6);
  not not_29 (o04, char7seg_5_o0);
  char7seg char7seg_5 (
    .c2(bit3_mux5to1_5_out_9[2]), .c1(bit3_mux5to1_5_out_9[1]), .c0(bit3_mux5to1_5_out_9[0]),
    .o0(char7seg_5_o0), .o1(char7seg_5_o1), .o2(char7seg_5_o2), .o3(char7seg_5_o3), .o4(char7seg_5_o4),
    .o5(char7seg_5_o5), .o6(char7seg_5_o6));
  not not_30 (o14, char7seg_5_o1);
  not not_31 (o24, char7seg_5_o2);
  not not_32 (o34, char7seg_5_o3);
  not not_33 (o44, char7seg_5_o4);
  not not_34 (o54, char7seg_5_o5);
  not not_35 (o64, char7seg_5_o6);
  not not_36 (o05, char7seg_6_o0);
  char7seg char7seg_6 (
    .c2(bit3_mux5to1_6_out_9[2]), .c1(bit3_mux5to1_6_out_9[1]), .c0(bit3_mux5to1_6_out_9[0]),
    .o0(char7seg_6_o0), .o1(char7seg_6_o1), .o2(char7seg_6_o2), .o3(char7seg_6_o3), .o4(char7seg_6_o4),
    .o5(char7seg_6_o5), .o6(char7seg_6_o6));
  not not_37 (o15, char7seg_6_o1);
  not not_38 (o25, char7seg_6_o2);
  not not_39 (o35, char7seg_6_o3);
  not not_40 (o45, char7seg_6_o4);
  not not_41 (o55, char7seg_6_o5);
  not not_42 (o65, char7seg_6_o6);
  not not_43 (o06, char7seg_7_o0);
  char7seg char7seg_7 (
    .c2(bit3_mux5to1_7_out_9[2]), .c1(bit3_mux5to1_7_out_9[1]), .c0(bit3_mux5to1_7_out_9[0]),
    .o0(char7seg_7_o0), .o1(char7seg_7_o1), .o2(char7seg_7_o2), .o3(char7seg_7_o3), .o4(char7seg_7_o4),
    .o5(char7seg_7_o5), .o6(char7seg_7_o6));
  not not_44 (o16, char7seg_7_o1);
  not not_45 (o26, char7seg_7_o2);
  not not_46 (o36, char7seg_7_o3);
  not not_47 (o46, char7seg_7_o4);
  not not_48 (o56, char7seg_7_o5);
  not not_49 (o66, char7seg_7_o6);
  not not_50 (o07, char7seg_8_o0);
  char7seg char7seg_8 (
    .c2(bit3_mux5to1_8_out_9[2]), .c1(bit3_mux5to1_8_out_9[1]), .c0(bit3_mux5to1_8_out_9[0]),
    .o0(char7seg_8_o0), .o1(char7seg_8_o1), .o2(char7seg_8_o2), .o3(char7seg_8_o3), .o4(char7seg_8_o4),
    .o5(char7seg_8_o5), .o6(char7seg_8_o6));
  not not_51 (o17, char7seg_8_o1);
  not not_52 (o27, char7seg_8_o2);
  not not_53 (o37, char7seg_8_o3);
  not not_54 (o47, char7seg_8_o4);
  not not_55 (o57, char7seg_8_o5);
  not not_56 (o67, char7seg_8_o6);
  _7_Segment_Display u_7_segment_display_1 (.g(o6), .f(o5), .a(o0), .b(o1), .e(o4), .d(o3), .c(o2), .dp(undriven));
  _7_Segment_Display u_7_segment_display_2 (
    .g(o61), .f(o51), .a(o01), .b(o11), .e(o41), .d(o31), .c(o21), .dp(undriven_2));
  _7_Segment_Display u_7_segment_display_3 (
    .g(o62), .f(o52), .a(o02), .b(o12), .e(o42), .d(o32), .c(o22), .dp(undriven_3));
  _7_Segment_Display u_7_segment_display_4 (
    .g(o63), .f(o53), .a(o03), .b(o13), .e(o43), .d(o33), .c(o23), .dp(undriven_4));
  _7_Segment_Display u_7_segment_display_5 (
    .g(o64), .f(o54), .a(o04), .b(o14), .e(o44), .d(o34), .c(o24), .dp(undriven_5));
  _7_Segment_Display u_7_segment_display_6 (
    .g(o65), .f(o55), .a(o05), .b(o15), .e(o45), .d(o35), .c(o25), .dp(undriven_6));
  _7_Segment_Display u_7_segment_display_7 (
    .g(o66), .f(o56), .a(o06), .b(o16), .e(o46), .d(o36), .c(o26), .dp(undriven_7));
  _7_Segment_Display u_7_segment_display_8 (
    .g(o67), .f(o57), .a(o07), .b(o17), .e(o47), .d(o37), .c(o27), .dp(undriven_8));
endmodule

module priority_encoder (
  input  a4,
  input  a3,
  input  a2,
  input  a1,
  input  a0,
  output y2,
  output y1,
  output y0
);

  wire and_1_out, and_2_out, and_3_out, and_4_out, not_1_out, not_2_out;

  not not_1 (not_1_out, a4);
  not not_2 (not_2_out, a2);
  and and_1 (and_1_out, not_1_out, a2);
  and and_2 (and_2_out, not_1_out, a3);
  and and_3 (and_3_out, not_1_out, a3);
  and and_4 (and_4_out, not_1_out, not_2_out, a1);
  or or_1 (y1, and_1_out, and_2_out);
  or or_2 (y0, and_3_out, and_4_out);

  assign y2 = a4;
endmodule
